// Logisim project ARM_CPU.circ as structural Verilog
module main (
);

  wire decode_1_rotate, decode_1_shift, decode_1_si, not_1_out;
  wire [1:0] decode_1_sop;
  wire [3:0] decode_1_cond, decode_1_rm, decode_1_rn, decode_1_rs;
  wire [4:0] decode_1_rtim, decode_1_sim, multiplexer_1_out, regfile_1_sv;
  wire [31:0] regfile_1_cpsrout;

  RegFile regfile_1 (
    .rM(decode_1_rm), .rN(decode_1_rn), .cpsrOut(regfile_1_cpsrout), .SV(regfile_1_sv), .rS(decode_1_rs));  // open: cpsrIn, S, W, WE, M, Clk, rW, N
  Multiplexer #(.width(5), .enable("false")) multiplexer_1 (
    .in0(regfile_1_sv), .in1(decode_1_sim), .out(multiplexer_1_out), .sel(not_1_out));
  not not_1 (not_1_out, decode_1_si);
  csprFlagDecode csprflagdecode_1 (.Cspr(regfile_1_cpsrout), .Cond(decode_1_cond));  // open: Execute
  Decode decode_1 (
    .SIm(decode_1_sim), .SI(decode_1_si), .Cond(decode_1_cond), .rN(decode_1_rn), .rS(decode_1_rs),
    .rM(decode_1_rm), .RtIm(decode_1_rtim), .SOp(decode_1_sop), .Shift(decode_1_shift),
    .Rotate(decode_1_rotate));  // open: rD, Op6, Op4, F, Inst, ST, I, S, Off, Im, ALUOp, RSB
  Multiplexer #(.width(5), .enable("false")) multiplexer_2 (
    .in0(multiplexer_1_out), .in1(decode_1_rtim), .sel(decode_1_rotate));  // open: out
  // OR_Gate or_1 has open pins: in0=decode_1_rotate, in1=decode_1_shift, out=open
endmodule

module Decode (
  input  [31:0] Inst,
  output [4:0] RtIm,
  output [3:0] Cond,
  output [1:0] F,
  output I,
  output [3:0] Op4,
  output S,
  output [5:0] Op6,
  output [3:0] rN,
  output [3:0] rD,
  output [3:0] rS,
  output [4:0] SIm,
  output [1:0] ST,
  output SI,
  output [3:0] rM,
  output [11:0] Off,
  output [7:0] Im,
  output Rotate,
  output [1:0] SOp,
  output Shift,
  output [3:0] ALUOp,
  output RSB
);

  wire and_1_out, and_3_out, and_4_out, and_5_out, decoder_1_out2, decoder_1_out4;
  wire [1:0] and_6_out, and_7_out, bit_extender_1_out, bit_extender_2_out;
  wire [3:0] not_1_out, not_4_out;
  wire [3:2] or_1_out;

  not not_1 (not_1_out[0], not_1_out[3]);
  not not_2 (not_1_out[1], not_1_out[3]);
  not not_3 (not_1_out[2], not_1_out[3]);
  Decoder #(.select(4), .enable("false")) decoder_1 (
    .out0(not_1_out[3]), .out1(not_4_out[3]), .out2(decoder_1_out2), .out3(RSB), .out4(decoder_1_out4),
    .sel(Inst[24:21]));  // open: out5, out6, out7, out8, out9, out10, out11, out12, out13, out14, out15
  not not_4 (not_4_out[0], not_4_out[3]);
  not not_5 (not_4_out[1], not_4_out[3]);
  or or_1 (or_1_out[2], decoder_1_out2, RSB);
  and and_1 (and_1_out, ~Inst[27], ~Inst[26], Inst[25]);  // AND_Gate
  and and_2 (Rotate, and_1_out, ~and_3_out);  // AND_Gate
  and and_3 (and_3_out, ~Inst[27], ~Inst[26], Inst[25], Inst[24], ~Inst[22], ~Inst[21], ~Inst[20]);  // AND_Gate
  and and_4 (and_4_out, ~Inst[27], ~Inst[26], ~Inst[25]);  // AND_Gate
  and and_5 (and_5_out, ~Inst[27], Inst[26], Inst[25]);  // AND_Gate
  not not_6 (or_1_out[3], or_1_out[2]);
  assign bit_extender_1_out = {{1{Rotate}}, Rotate};  // Bit_Extender bit_extender_1
  assign bit_extender_2_out = {{1{Shift}}, Shift};  // Bit_Extender bit_extender_2
  or or_2 (Shift, and_4_out, and_5_out);
  not not_7 (RtIm[0], Inst[25]);
  assign and_6_out = bit_extender_1_out & {2{Rotate}};  // AND_Gate and_6, 2 bits wide
  assign and_7_out = Inst[6:5] & bit_extender_2_out;  // AND_Gate and_7, 2 bits wide
  assign SOp = and_6_out | and_7_out;  // OR_Gate or_3, 2 bits wide
  assign ALUOp = not_1_out | {{2{not_4_out[3]}}, not_4_out[1:0]} | {or_1_out, {2{or_1_out[2]}}};  // OR_Gate or_4, 4 bits wide

  assign Cond = Inst[31:28];
  assign F = Inst[27:26];
  assign I = Inst[25];
  assign Im = Inst[7:0];
  assign Off = Inst[11:0];
  assign Op4 = Inst[24:21];
  assign Op6 = Inst[25:20];
  assign rD = Inst[15:12];
  assign rM = Inst[3:0];
  assign rN = Inst[19:16];
  assign rS = Inst[11:8];
  assign RtIm[4:1] = Inst[11:8];
  assign S = Inst[20];
  assign SI = Inst[4];
  assign SIm = Inst[11:7];
  assign ST = Inst[6:5];

  // Other names for the same wires on the sheet: DestReg[3:0] = Inst[15:12]; Format[1:0] = Inst[27:26];
  //   InputReg[3:0] = Inst[19:16]; SCF = Inst[20]; OpCode[3:0] = Inst[24:21]; Operand2[11:0] = Inst[11:0];
  //   SOp_t[1:0] = Inst[6:5]

  // Notes on the sheet:
  //   operand 2
  //   rd
  //   rn
  //   set cond flags
  //   op code
  //   immediate
  //   format
  //   conditional
endmodule

module RegFile (
  input  [31:0] cpsrIn,
  input  S,
  input  [31:0] W,
  input  WE,
  input  Clk,
  input  [3:0] rM,
  input  [3:0] rW,
  input  [3:0] rN,
  input  [3:0] rS,
  output [31:0] cpsrOut,
  output [31:0] M,
  output [31:0] N,
  output [4:0] SV
);

  wire and_1_out, and_2_out, and_3_out, and_4_out, and_5_out, and_6_out, and_7_out, and_8_out, and_9_out,
       and_10_out, and_11_out, and_12_out, and_13_out, and_14_out, and_15_out, and_16_out, r0, r1, r2, r3,
       r4, r5, r6, r7, r8, r9, r10, r11, r12, r13, r14, r15;
  wire [31:0] a1, a2, a3, a4, ip, lr, pc, sp, v1, v2, v3, v4, v5, v6, v7, v8;
  wire [31:5] multiplexer_3_out;

  Decoder #(.select(4), .enable("false")) decoder_1 (
    .out0(r0), .out1(r1), .out2(r2), .out3(r3), .out4(r4), .out5(r5), .out6(r6), .out7(r7), .out8(r8),
    .out9(r9), .out10(r10), .out11(r11), .out12(r12), .out13(r13), .out14(r14), .out15(r15), .sel(rW));
  Register #(.width(32)) cpsr (.D(cpsrIn), .en(S), .clk(Clk), .Q(cpsrOut));  // open: clr
  Register #(.width(32)) u_a1 (.D(W), .en(and_1_out), .clk(Clk), .Q(a1));  // open: clr
  and and_1 (and_1_out, WE, r0);
  Register #(.width(32)) u_a2 (.D(W), .en(and_2_out), .clk(Clk), .Q(a2));  // open: clr
  and and_2 (and_2_out, WE, r1);
  Register #(.width(32)) u_a3 (.D(W), .en(and_3_out), .clk(Clk), .Q(a3));  // open: clr
  and and_3 (and_3_out, WE, r2);
  Register #(.width(32)) u_a4 (.D(W), .en(and_4_out), .clk(Clk), .Q(a4));  // open: clr
  and and_4 (and_4_out, WE, r3);
  Register #(.width(32)) u_v1 (.D(W), .en(and_5_out), .clk(Clk), .Q(v1));  // open: clr
  and and_5 (and_5_out, WE, r4);
  Register #(.width(32)) u_v2 (.D(W), .en(and_6_out), .clk(Clk), .Q(v2));  // open: clr
  and and_6 (and_6_out, WE, r5);
  Register #(.width(32)) u_v3 (.D(W), .en(and_7_out), .clk(Clk), .Q(v3));  // open: clr
  and and_7 (and_7_out, WE, r6);
  Register #(.width(32)) u_v4 (.D(W), .en(and_8_out), .clk(Clk), .Q(v4));  // open: clr
  and and_8 (and_8_out, WE, r7);
  Register #(.width(32)) u_v5 (.D(W), .en(and_9_out), .clk(Clk), .Q(v5));  // open: clr
  and and_9 (and_9_out, WE, r8);
  Register #(.width(32)) u_v6 (.D(W), .en(and_10_out), .clk(Clk), .Q(v6));  // open: clr
  and and_10 (and_10_out, WE, r9);
  Register #(.width(32)) u_v7 (.D(W), .en(and_11_out), .clk(Clk), .Q(v7));  // open: clr
  and and_11 (and_11_out, WE, r10);
  Register #(.width(32)) u_v8 (.D(W), .en(and_12_out), .clk(Clk), .Q(v8));  // open: clr
  and and_12 (and_12_out, WE, r11);
  Register #(.width(32)) u_ip (.D(W), .en(and_13_out), .clk(Clk), .Q(ip));  // open: clr
  and and_13 (and_13_out, WE, r12);
  Register #(.width(32)) u_sp (.D(W), .en(and_14_out), .clk(Clk), .Q(sp));  // open: clr
  and and_14 (and_14_out, WE, r13);
  Register #(.width(32)) u_lr (.D(W), .en(and_15_out), .clk(Clk), .Q(lr));  // open: clr
  and and_15 (and_15_out, WE, r14);
  Register #(.width(32)) u_pc (.D(W), .en(and_16_out), .clk(Clk), .Q(pc));  // open: clr
  and and_16 (and_16_out, WE, r15);
  Multiplexer #(.select(4), .width(32), .enable("false")) multiplexer_1 (
    .in0(a1), .in1(a2), .in2(a3), .in3(a4), .in4(v1), .in5(v2), .in6(v3), .in7(v4), .in8(v5), .in9(v6),
    .in10(v7), .in11(v8), .in12(ip), .in13(sp), .in14(lr), .in15(pc), .out(M), .sel(rM));
  Multiplexer #(.select(4), .width(32), .enable("false")) multiplexer_2 (
    .in0(a1), .in1(a2), .in2(a3), .in3(a4), .in4(v1), .in5(v2), .in6(v3), .in7(v4), .in8(v5), .in9(v6),
    .in10(v7), .in11(v8), .in12(ip), .in13(sp), .in14(lr), .in15(pc), .out(N), .sel(rN));
  Multiplexer #(.select(4), .width(32), .enable("false")) multiplexer_3 (
    .in0(a1), .in1(a2), .in2(a3), .in3(a4), .in4(v1), .in5(v2), .in6(v3), .in7(v4), .in8(v5), .in9(v6),
    .in10(v7), .in11(v8), .in12(ip), .in13(sp), .in14(lr), .in15(pc), .out({multiplexer_3_out, SV}), .sel(rS));
endmodule

module csprFlagDecode (
  input  [31:0] Cspr,
  input  [3:0] Cond,
  output Execute
);

  wire AL, and_1_out, and_2_out, and_3_out, and_4_out, and_5_out, and_6_out, and_7_out, and_8_out, and_9_out,
       and_10_out, and_11_out, and_12_out, and_13_out, and_14_out, EQ, GE, GT, HI, HS, LE, LO, LS, LT, MI,
       NE, NV, or_1_out, or_2_out, or_3_out, or_4_out, or_5_out, or_6_out, or_7_out, or_8_out, or_9_out,
       or_10_out, or_11_out, or_12_out, or_13_out, PL, VC, VS;

  Decoder #(.select(4), .enable("false")) decoder_1 (
    .out0(EQ), .out1(NE), .out2(HS), .out3(LO), .out4(MI), .out5(PL), .out6(VS), .out7(VC), .out8(HI),
    .out9(LS), .out10(GE), .out11(LT), .out12(GT), .out13(LE), .out14(AL), .out15(NV), .sel(Cond));
  and and_1 (and_1_out, EQ, Cspr[30]);
  and and_2 (and_2_out, NE, ~Cspr[30]);  // AND_Gate
  and and_3 (and_3_out, HS, Cspr[29]);
  and and_4 (and_4_out, LO, ~Cspr[29]);  // AND_Gate
  and and_5 (and_5_out, MI, Cspr[31]);
  and and_6 (and_6_out, PL, ~Cspr[31]);  // AND_Gate
  and and_7 (and_7_out, VS, Cspr[28]);
  and and_8 (and_8_out, VC, ~Cspr[28]);  // AND_Gate
  and and_9 (and_9_out, HI, Cspr[29], ~Cspr[30]);  // AND_Gate
  or or_1 (or_1_out, ~Cspr[29], Cspr[30]);  // OR_Gate
  or or_2 (or_2_out, Cspr[28], Cspr[31]);
  or or_3 (or_3_out, ~Cspr[28], ~Cspr[31]);  // OR_Gate
  or or_4 (or_4_out, ~Cspr[28], Cspr[31]);  // OR_Gate
  or or_5 (or_5_out, Cspr[28], ~Cspr[31]);  // OR_Gate
  or or_6 (or_6_out, Cspr[28], ~Cspr[30], Cspr[31]);  // OR_Gate
  or or_7 (or_7_out, ~Cspr[28], ~Cspr[30], ~Cspr[31]);  // OR_Gate
  or or_8 (or_8_out, ~Cspr[28], Cspr[30], Cspr[31]);  // OR_Gate
  or or_9 (or_9_out, Cspr[28], Cspr[30], ~Cspr[31]);  // OR_Gate
  and and_10 (and_10_out, or_1_out, LS);
  or or_10 (or_10_out, or_2_out, or_3_out);
  or or_11 (or_11_out, or_4_out, or_5_out);
  or or_12 (or_12_out, or_6_out, or_7_out);
  or or_13 (or_13_out, or_8_out, or_9_out);
  and and_11 (and_11_out, or_10_out, GE);
  and and_12 (and_12_out, or_11_out, LT);
  and and_13 (and_13_out, or_12_out, GT);
  and and_14 (and_14_out, or_13_out, LE);
  or or_14 (Execute, and_1_out, and_2_out, and_3_out, and_4_out, and_5_out, and_6_out, and_7_out, and_8_out, and_9_out, and_10_out, and_11_out, and_12_out, and_13_out, and_14_out, AL);

  // Other names for the same wires on the sheet: b0 = Cspr[28]; b1 = Cspr[29]; b2 = Cspr[30]; b3 = Cspr[31]
endmodule

module Shift32 (
  input  [31:0] M,
  input  [4:0] Shift,
  input  [1:0] SOp,
  output [31:0] Mout
);

  wire and_1_out, and_2_out, multiplexer_1_out, or_1_out;
  wire [31:0] leftshift_1_mout, multiplexer_2_out, switchbit_1_aout, switchbit_2_aout;

  SwitchBit switchbit_1 (.A(M), .Aout(switchbit_1_aout));
  Multiplexer #(.enable("false")) multiplexer_1 (.in0(SOp[1]), .in1(M[31]), .out(multiplexer_1_out), .sel(and_1_out));
  and and_1 (and_1_out, SOp[1], ~SOp[0]);  // AND_Gate
  Multiplexer #(.width(32), .enable("false")) multiplexer_2 (
    .in0(M), .in1(switchbit_1_aout), .out(multiplexer_2_out), .sel(or_1_out));
  or or_1 (or_1_out, SOp[1], SOp[1]);
  and and_2 (and_2_out, SOp[0], SOp[1]);
  LeftShift leftshift_1 (
    .M(multiplexer_2_out), .in_2(multiplexer_1_out), .in_3(and_2_out), .Shift(Shift), .Mout(leftshift_1_mout));
  Multiplexer #(.width(32), .enable("false")) multiplexer_3 (
    .in0(leftshift_1_mout), .in1(switchbit_2_aout), .out(Mout), .sel(or_1_out));
  SwitchBit switchbit_2 (.A(leftshift_1_mout), .Aout(switchbit_2_aout));

  // Notes on the sheet:
  //   Most Significant Bit
endmodule

module LeftShift (
  input  [31:0] M,
  input  in_2,
  input  in_3,
  input  [4:0] Shift,
  output [31:0] Mout
);

  wire [31:0] l2_1_mout, l4_1_mout, l8_1_mout, l16_1_mout;

  L16 l16_1 (.M(M), .Shift(Shift[4]), .Cin(in_2), .SOp(in_3), .Mout(l16_1_mout));
  L8 l8_1 (.M(l16_1_mout), .Shift(Shift[3]), .Cin(in_2), .SOp(in_3), .Mout(l8_1_mout));
  L4 l4_1 (.M(l8_1_mout), .Shift(Shift[2]), .Cin(in_2), .SOp(in_3), .Mout(l4_1_mout));
  L2 l2_1 (.M(l4_1_mout), .Shift(Shift[1]), .Cin(in_2), .SOp(in_3), .Mout(l2_1_mout));
  L1 l1_1 (.M(l2_1_mout), .Shift(Shift[0]), .Cin(in_2), .SOp(in_3), .Mout(Mout));

  // Other names for the same wires on the sheet: Cin = in_2; SOp = in_3

  // Notes on the sheet:
  //   Do not delete or rename any of the input or output pins, and do not add any other pins.
  //   (It's fine to move them around, though)
endmodule

module L1 (
  input  [31:0] M,
  input  Shift,
  input  Cin,
  input  SOp,
  output [31:0] Mout
);

  wire [0:0] multiplexer_1_out;

  Multiplexer #(.enable("false")) multiplexer_1 (.in0(Cin), .in1(M[31]), .out(multiplexer_1_out[0]), .sel(SOp));
  Multiplexer #(.width(32), .enable("false")) multiplexer_2 (
    .in0(M), .in1({M[30:0], multiplexer_1_out[0]}), .out(Mout), .sel(Shift));
endmodule

module L2 (
  input  [31:0] M,
  input  Shift,
  input  Cin,
  input  SOp,
  output [31:0] Mout
);

  wire [1:0] bit_extender_1_out, multiplexer_1_out;

  assign bit_extender_1_out = {{1{Cin}}, Cin};  // Bit_Extender bit_extender_1
  Multiplexer #(.width(2), .enable("false")) multiplexer_1 (
    .in0(bit_extender_1_out), .in1({M[30], M[31]}), .out(multiplexer_1_out), .sel(SOp));
  Multiplexer #(.width(32), .enable("false")) multiplexer_2 (
    .in0(M), .in1({M[29:0], multiplexer_1_out[0], multiplexer_1_out[1]}), .out(Mout), .sel(Shift));
endmodule

module L4 (
  input  [31:0] M,
  input  Shift,
  input  Cin,
  input  SOp,
  output [31:0] Mout
);

  wire [3:0] bit_extender_1_out, multiplexer_1_out;

  assign bit_extender_1_out = {{3{Cin}}, Cin};  // Bit_Extender bit_extender_1
  Multiplexer #(.width(4), .enable("false")) multiplexer_1 (
    .in0(bit_extender_1_out), .in1({M[28], M[29], M[30], M[31]}), .out(multiplexer_1_out), .sel(SOp));
  Multiplexer #(.width(32), .enable("false")) multiplexer_2 (
    .in0(M),
    .in1({M[27:0], multiplexer_1_out[0], multiplexer_1_out[1], multiplexer_1_out[2], multiplexer_1_out[3]}),
    .out(Mout), .sel(Shift));
endmodule

module L8 (
  input  [31:0] M,
  input  Shift,
  input  Cin,
  input  SOp,
  output [31:0] Mout
);

  wire [7:0] bit_extender_1_out, multiplexer_1_out;

  assign bit_extender_1_out = {{7{Cin}}, Cin};  // Bit_Extender bit_extender_1
  Multiplexer #(.width(8), .enable("false")) multiplexer_1 (
    .in0(bit_extender_1_out), .in1({M[24], M[25], M[26], M[27], M[28], M[29], M[30], M[31]}),
    .out(multiplexer_1_out), .sel(SOp));
  Multiplexer #(.width(32), .enable("false")) multiplexer_2 (
    .in0(M),
    .in1({M[23:0], multiplexer_1_out[0], multiplexer_1_out[1], multiplexer_1_out[2], multiplexer_1_out[3], multiplexer_1_out[4], multiplexer_1_out[5], multiplexer_1_out[6], multiplexer_1_out[7]}),
    .out(Mout), .sel(Shift));
endmodule

module L16 (
  input  [31:0] M,
  input  Shift,
  input  Cin,
  input  SOp,
  output [31:0] Mout
);

  wire [15:0] bit_extender_1_out, multiplexer_1_out;

  assign bit_extender_1_out = {{15{Cin}}, Cin};  // Bit_Extender bit_extender_1
  Multiplexer #(.width(16), .enable("false")) multiplexer_1 (
    .in0(bit_extender_1_out),
    .in1({M[16], M[17], M[18], M[19], M[20], M[21], M[22], M[23], M[24], M[25], M[26], M[27], M[28], M[29], M[30], M[31]}),
    .out(multiplexer_1_out), .sel(SOp));
  Multiplexer #(.width(32), .enable("false")) multiplexer_2 (
    .in0(M),
    .in1({M[15:0], multiplexer_1_out[0], multiplexer_1_out[1], multiplexer_1_out[2], multiplexer_1_out[3], multiplexer_1_out[4], multiplexer_1_out[5], multiplexer_1_out[6], multiplexer_1_out[7], multiplexer_1_out[8], multiplexer_1_out[9], multiplexer_1_out[10], multiplexer_1_out[11], multiplexer_1_out[12], multiplexer_1_out[13], multiplexer_1_out[14], multiplexer_1_out[15]}),
    .out(Mout), .sel(Shift));
endmodule

module SwitchBit (
  input  [31:0] A,
  output [31:0] Aout
);


  assign Aout = {A[0], A[1], A[2], A[3], A[4], A[5], A[6], A[7], A[8], A[9], A[10], A[11], A[12], A[13], A[14], A[15], A[16], A[17], A[18], A[19], A[20], A[21], A[22], A[23], A[24], A[25], A[26], A[27], A[28], A[29], A[30], A[31]};
endmodule
